// Logisim project D-FlipFlopUsingNor.circ as structural Verilog: 1 circuit, main circuit main
module main (
  input  in_1,
  output out_2,
  output out_3
);

  wire and_1_out, and_2_out, clock_1_out, not_1_out;

  Clock clock_1 (.out(clock_1_out));
  not not_1 (not_1_out, in_1);
  and and_1 (and_1_out, clock_1_out, not_1_out);
  and and_2 (and_2_out, in_1, clock_1_out);
  nor nor_1 (out_2, and_2_out, out_3);
  xor xor_1 (out_3, out_2, and_1_out);
endmodule
